# Fritzing sketch Pico Wiring (saved by Fritzing 1.0.5)
breadboards: 1

parts:
  OLED1 = SSD1306 0.96in 128x64 I2C Monochrome OLED Display
  Mod1 = Raspberry Pi Pico
  U1 = RJ45 Jack [package=rj45-8]
  JP1 = Header 8 [package=1x08_smd_combined]

nets:
  N1: OLED1.GND, Mod1.pin_3, Mod1.pin_8, Mod1.pin_13, Mod1.pin_18, Mod1.pin_23, Mod1.pin_28, Mod1.pin_33, Mod1.pin_38, Mod1.pin_42, U1.4, JP1.4
  N2: OLED1.VCC, Mod1.pin_36
  N3: OLED1.SCL, Mod1.pin_27
  N4: OLED1.SDA, Mod1.pin_26
  N5: Mod1.pin_21, U1.8, JP1.8
  N6: Mod1.pin_22, U1.1, JP1.1

custom parts:
  Raspberry Pi Pico: Raspberry Pi Pico. Based around the RP2040 microcontroller the Pico is a low cost microcontroller device bringing Raspberry Pi quality, cost, and easy of use to the microcontroller space. Jan 2021, Split part in to two versions: tht (this one) and SMD. This one will drill holes for a .1 in header in pcb to allow plugging in the module as well as providing pads to solder the module to the top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
